# Fritzing sketch breadboard-modelB (saved by Fritzing 0.9.0b)
breadboards: 1

parts:
  Raspberry_Pi_B_rev1 = Raspberry Pi B rev1
  LED1 = LED - 3mm [color="Red (633nm)" package="3 mm [THT]"]
  R1 = Resistor [package="0402 [SMD]"]
  S1 = Momentary Switch [package=ksa_sealed_tac_switch]
  S2 = Momentary Switch [package=ksa_sealed_tac_switch]

nets:
  N1: Raspberry_Pi_B_rev1.GPIO_0, S1.4
  N2: Raspberry_Pi_B_rev1.GPIO_1, S2.4
  N3: Raspberry_Pi_B_rev1.GND, R1.Pin_1, S1.2, S2.2
  N4: Raspberry_Pi_B_rev1.GPIO_11, LED1.cathode
  N5: LED1.anode, R1.Pin_0
